// Logisim project AsteroidPong.circ as structural Verilog: 7 circuits, main circuit main
module main (
  input  in_1,
  input  in_2,
  output out_3
);

  wire _128_HZ_out, reductordefrecuencia_1_clock_salida;
  wire [6:0] keyboard_1_data;
  wire [31:0] worldprocess_1_f0, worldprocess_1_f1, worldprocess_1_f2, worldprocess_1_f3, worldprocess_1_f4,
       worldprocess_1_f5, worldprocess_1_f6, worldprocess_1_f7, worldprocess_1_f8, worldprocess_1_f9,
       worldprocess_1_f10, worldprocess_1_f11, worldprocess_1_f12, worldprocess_1_f13, worldprocess_1_f14,
       worldprocess_1_f15, worldprocess_1_f16, worldprocess_1_f17, worldprocess_1_f18, worldprocess_1_f19,
       worldprocess_1_f20, worldprocess_1_f21, worldprocess_1_f22, worldprocess_1_f23, worldprocess_1_f24,
       worldprocess_1_f25, worldprocess_1_f26, worldprocess_1_f27, worldprocess_1_f28, worldprocess_1_f29,
       worldprocess_1_f30, worldprocess_1_player;

  Clock _128_HZ (.out(_128_HZ_out));
  Keyboard keyboard_1 (.clk(_128_HZ_out), .re(in_1), .clr(in_2), .avail(out_3), .data(keyboard_1_data));
  ReductorDeFrecuencia reductordefrecuencia_1 (
    .Clock_Entrada(_128_HZ_out), .Clock_salida(reductordefrecuencia_1_clock_salida));
  WorldProcess worldprocess_1 (
    .teclado(keyboard_1_data), .reloj(reductordefrecuencia_1_clock_salida), .F0(worldprocess_1_f0),
    .F1(worldprocess_1_f1), .F2(worldprocess_1_f2), .F3(worldprocess_1_f3), .F4(worldprocess_1_f4),
    .F5(worldprocess_1_f5), .F6(worldprocess_1_f6), .F7(worldprocess_1_f7), .F8(worldprocess_1_f8),
    .F9(worldprocess_1_f9), .F10(worldprocess_1_f10), .F11(worldprocess_1_f11), .F12(worldprocess_1_f12),
    .F13(worldprocess_1_f13), .F14(worldprocess_1_f14), .F15(worldprocess_1_f15), .F16(worldprocess_1_f16),
    .F17(worldprocess_1_f17), .F18(worldprocess_1_f18), .F19(worldprocess_1_f19), .F20(worldprocess_1_f20),
    .F21(worldprocess_1_f21), .F22(worldprocess_1_f22), .F23(worldprocess_1_f23), .F24(worldprocess_1_f24),
    .F25(worldprocess_1_f25), .F26(worldprocess_1_f26), .F27(worldprocess_1_f27), .F28(worldprocess_1_f28),
    .F29(worldprocess_1_f29), .F30(worldprocess_1_f30), .Player(worldprocess_1_player));
  DotMatrix #(.inputtype("row"), .matrixcols(32), .matrixrows(32)) dotmatrix_1 (
    .row0(worldprocess_1_f0), .row1(worldprocess_1_f1), .row2(worldprocess_1_f2), .row3(worldprocess_1_f3),
    .row4(worldprocess_1_f4), .row5(worldprocess_1_f5), .row6(worldprocess_1_f6), .row7(worldprocess_1_f7),
    .row8(worldprocess_1_f8), .row9(worldprocess_1_f9), .row10(worldprocess_1_f10),
    .row11(worldprocess_1_f11), .row12(worldprocess_1_f12), .row13(worldprocess_1_f13),
    .row14(worldprocess_1_f14), .row15(worldprocess_1_f15), .row16(worldprocess_1_f16),
    .row17(worldprocess_1_f17), .row18(worldprocess_1_f18), .row19(worldprocess_1_f19),
    .row20(worldprocess_1_f20), .row21(worldprocess_1_f21), .row22(worldprocess_1_f22),
    .row23(worldprocess_1_f23), .row24(worldprocess_1_f24), .row25(worldprocess_1_f25),
    .row26(worldprocess_1_f26), .row27(worldprocess_1_f27), .row28(worldprocess_1_f28),
    .row29(worldprocess_1_f29), .row30(worldprocess_1_f30), .row31(worldprocess_1_player));
endmodule

module Player (
  input  [6:0] in_1,
  output [31:0] out_2
);

  wire comparator_1_eq, comparator_2_eq, playermovselect_1_anterior, playermovselect_1_siguiente;
  wire [4:0] counter_1_q;

  Comparator #(.width(7), .mode("unsigned")) comparator_1 (
    .a(7'b1100001), .b(in_1), .eq(comparator_1_eq));  // open: gt, lt
  Comparator #(.width(7), .mode("unsigned")) comparator_2 (
    .a(7'b1100100), .b(in_1), .eq(comparator_2_eq));  // open: gt, lt
  PlayerMovSelect playermovselect_1 (
    .a(comparator_1_eq), .d(comparator_2_eq), .anterior(playermovselect_1_anterior),
    .siguiente(playermovselect_1_siguiente));
  PlayerMovement playermovement_1 (.in_1(counter_1_q), .out_2(out_2));
  Counter #(.width(5), .max('h1f)) counter_1 (
    .load(playermovselect_1_anterior), .Q(counter_1_q), .clk(playermovselect_1_siguiente));  // open: D, count, carry, clr
endmodule

module PlayerMovSelect (
  input  a,
  input  d,
  output anterior,
  output siguiente
);

  wire and_2_out, and_3_out, not_1_out, not_2_out, not_3_out;

  not not_1 (not_1_out, d);
  not not_2 (not_2_out, a);
  not not_3 (not_3_out, d);
  and and_1 (anterior, a, not_1_out);
  and and_2 (and_2_out, not_2_out, d);
  and and_3 (and_3_out, a, not_3_out);
  or or_1 (siguiente, and_2_out, and_3_out);
endmodule

// at
module RandomSystem (
  input  reloj,
  output [31:0] out_2
);

  wire [2:0] random_1_out, random_2_out, random_3_out;
  wire [7:0] decoder_1_out7, decoder_2_out7, decoder_3_out7;

  Random #(.width(3)) random_1 (.clk(reloj), .next(1'b1), .out(random_1_out));  // open: clr
  Random #(.width(3)) random_2 (.clk(reloj), .next(1'b1), .out(random_2_out));  // open: clr
  Random #(.width(3)) random_3 (.clk(reloj), .next(1'b1), .out(random_3_out));  // open: clr
  Decoder #(.select(3)) decoder_1 (
    .out0(decoder_1_out7[7]), .out1(decoder_1_out7[6]), .out2(decoder_1_out7[5]), .out3(decoder_1_out7[4]),
    .out4(decoder_1_out7[3]), .out5(decoder_1_out7[2]), .out6(decoder_1_out7[1]), .out7(decoder_1_out7[0]),
    .sel(random_1_out));  // open: en
  Decoder #(.select(3)) decoder_2 (
    .out0(decoder_2_out7[7]), .out1(decoder_2_out7[6]), .out2(decoder_2_out7[5]), .out3(decoder_2_out7[4]),
    .out4(decoder_2_out7[3]), .out5(decoder_2_out7[2]), .out6(decoder_2_out7[1]), .out7(decoder_2_out7[0]),
    .sel(random_2_out));  // open: en
  Decoder #(.select(3)) decoder_3 (
    .out0(decoder_3_out7[7]), .out1(decoder_3_out7[6]), .out2(decoder_3_out7[5]), .out3(decoder_3_out7[4]),
    .out4(decoder_3_out7[3]), .out5(decoder_3_out7[2]), .out6(decoder_3_out7[1]), .out7(decoder_3_out7[0]),
    .sel(random_3_out));  // open: en
  assign out_2[10:0] = {{3{1'b0}}, decoder_1_out7};  // Bit_Extender bit_extender_1
  assign out_2[21:11] = {{3{1'b0}}, decoder_3_out7};  // Bit_Extender bit_extender_2
  assign out_2[31:22] = {{2{1'b0}}, decoder_2_out7};  // Bit_Extender bit_extender_3
endmodule

module PlayerMovement (
  input  [4:0] in_1,
  output [31:0] out_2
);

  Multiplexer #(.select(5), .width(32)) multiplexer_1 (
    .in0(32'he0000000), .in1(32'h70000000), .in2(32'h38000000), .in3(32'h1c000000), .in4(32'he000000),
    .in5(32'h7000000), .in6(32'h3800000), .in7(32'h1c00000), .in8(32'he00000), .in9(32'h700000),
    .in10(32'h380000), .in11(32'h1c0000), .in12(32'he0000), .in13(32'h70000), .in14(32'h38000),
    .in15(32'h1c000), .in16(32'he000), .in17(32'h7000), .in18(32'h3800), .in19(32'h1c00), .in20(32'he00),
    .in21(32'h700), .in22(32'h380), .in23(32'h1c0), .in24(32'he0), .in25(32'h70), .in26(32'h38),
    .in27(32'h1c), .in28(32'he), .in29(32'h7), .in30(32'h80000003), .in31(32'hc0000001), .out(out_2),
    .sel(in_1));  // open: en
endmodule

module WorldProcess (
  input  reloj,
  input  [6:0] teclado,
  output [31:0] F0,
  output [31:0] F1,
  output [31:0] F2,
  output [31:0] F3,
  output [31:0] F4,
  output [31:0] F5,
  output [31:0] F6,
  output [31:0] F7,
  output [31:0] F8,
  output [31:0] F9,
  output [31:0] F10,
  output [31:0] F11,
  output [31:0] F12,
  output [31:0] F13,
  output [31:0] F14,
  output [31:0] F15,
  output [31:0] F16,
  output [31:0] F17,
  output [31:0] F18,
  output [31:0] F19,
  output [31:0] F20,
  output [31:0] F21,
  output [31:0] F22,
  output [31:0] F23,
  output [31:0] F24,
  output [31:0] F25,
  output [31:0] F26,
  output [31:0] F27,
  output [31:0] F28,
  output [31:0] F29,
  output [31:0] F30,
  output [31:0] Player
);

  wire counter_1_carry;
  wire [4:0] counter_1_q;
  wire [31:0] randomsystem_1_out_2;

  Counter #(.width(5), .max('h1f)) counter_1 (
    .Q(counter_1_q), .carry(counter_1_carry), .clk(reloj));  // open: load, D, count, clr
  RandomSystem randomsystem_1 (.reloj(counter_1_carry), .out_2(randomsystem_1_out_2));
  Demultiplexer #(.select(5), .width(32)) demultiplexer_1 (
    .out0(F0), .out1(F1), .out2(F2), .out3(F3), .out4(F4), .out5(F5), .out6(F6), .out7(F7), .out8(F8),
    .out9(F9), .out10(F10), .out11(F11), .out12(F12), .out13(F13), .out14(F14), .out15(F15), .out16(F16),
    .out17(F17), .out18(F18), .out19(F19), .out20(F20), .out21(F21), .out22(F22), .out23(F23), .out24(F24),
    .out25(F25), .out26(F26), .out27(F27), .out28(F28), .out29(F29), .out30(F30), .in(randomsystem_1_out_2),
    .sel(counter_1_q));  // open: out31, en
  Player player_1 (.in_1(teclado), .out_2(Player));
endmodule

module ReductorDeFrecuencia (
  input  Clock_Entrada,
  output Clock_salida
);

  wire j_k_ff_1_q, j_k_ff_2_q;

  J_K_Flip_Flop j_k_ff_1 (.J(1'b1), .clk(Clock_Entrada), .K(1'b1), .Q(j_k_ff_1_q));  // open: Qn, preset, en, reset
  J_K_Flip_Flop j_k_ff_2 (.J(1'b1), .clk(j_k_ff_1_q), .K(1'b1), .Q(j_k_ff_2_q));  // open: Qn, preset, en, reset
  J_K_Flip_Flop j_k_ff_3 (.J(1'b1), .clk(j_k_ff_2_q), .K(1'b1), .Q(Clock_salida));  // open: Qn, preset, en, reset
endmodule
